// Logisim project circuit.circ as structural Verilog: 35 circuits, main circuit RegFile
module main (
);

  wire branch_1_branch, button_1_out, button_2_out, ctrl_decoder_1_branch, ctrl_decoder_1_jal,
       ctrl_decoder_1_jalr, ctrl_decoder_1_m_rd, ctrl_decoder_2_1_m_rd, ctrl_decoder_2_1_m_wr,
       ctrl_decoder_2_1_rf_wr, ctrl_decoder_3_1_rf_wr, main_1_dflush, main_1_dstall, main_1_eflush,
       main_1_fstall, main_2_branch, main_2_jal, main_2_jalr, main_2_m_rd, main_2_m_wr, main_2_rf_wr,
       or_1_out, or_2_out;
  wire [1:0] ctrl_decoder_1_a_sel, ctrl_decoder_1_alu_op, ctrl_decoder_1_b_sel, ctrl_decoder_3_1_wb_sel,
       forwarding_unit_1_a_fwd, forwarding_unit_1_b_fwd, main_2_a_sel, main_2_alu_op, main_2_b_sel,
       main_2_wb_sel;
  wire [2:0] alu_control_1_op, instr_decoder_2_1_funct3;
  wire [4:0] decoder_1_rs1, decoder_1_rs2, EX_MEM_out_9, instr_decoder_2_1_rd, instr_decoder_2_1_rs1,
       instr_decoder_2_1_rs2, MEM_WB_out_9;
  wire [6:0] decoder_1_opcode;
  wire [31:0] A_ADD_Imm_out_3, alu_mux_1_out_5, alu_mux_2_out_5, control_mux_1_out_4, ctrl_encode_1_out_11,
       data_mem_1_out_5, EX_MEM_out_6, EX_MEM_out_7, EX_MEM_out_8, fwd_mux_1_out_5, fwd_mux_2_out_5,
       ID_EX_a_2, ID_EX_b_2, ID_EX_ctrl_2, ID_EX_imm_2, ID_EX_ire_2, ID_EX_pce_2, IF_ID_instr_out,
       IF_ID_pc_out, immgen_1_imm, instr_mem_1_out_3, instr_mux_1_out_4, jumpaddr_1_out_4, main_3_rd0,
       main_3_rd1, main_4_out, MEM_WB_out_6, MEM_WB_out_7, MEM_WB_out_8, pc_1_out, pc_add_4_1_out_3,
       PC_ADD_Imm_out_3, rf_mux_1_out_4, rf_mux_2_out_4, zero_1_out_2;

  RF_MUX rf_mux_1 (.in_1(jumpaddr_1_out_4), .out_4(rf_mux_1_out_4), .in_2(pc_add_4_1_out_3), .in_3(or_1_out));
  Button button_1 (.out(button_1_out));
  Button button_2 (.out(button_2_out));
  PC pc_1 (.in(rf_mux_1_out_4), .clear(button_1_out), .hold(main_1_fstall), .out(pc_1_out), .clk(button_2_out));
  PC_ADD_4 pc_add_4_1 (.in_2(3'b100), .in_1(pc_1_out), .out_3(pc_add_4_1_out_3));
  instr_MEM instr_mem_1 (.in_1(pc_1_out), .out_3(instr_mem_1_out_3), .in_2(button_2_out));
  or or_1 (or_1_out, branch_1_branch, or_2_out);
  Instr_MUX instr_mux_1 (.in_2(1'b0), .in_1(instr_mem_1_out_3), .sel(main_1_dflush), .out_4(instr_mux_1_out_4));
  IF_ID IF_ID (
    .pc_in(pc_1_out), .instr_in(instr_mux_1_out_4), .hold(main_1_dstall), .clear(main_1_dflush),
    .pc_out(IF_ID_pc_out), .instr_out(IF_ID_instr_out), .clk(button_2_out));
  hazardunit_main main_1 (
    .branch(branch_1_branch), .m_rd_e(ctrl_decoder_1_m_rd), .jump(or_2_out), .rs1(decoder_1_rs1),
    .rs2(decoder_1_rs2), .rde(instr_decoder_2_1_rd), .dstall(main_1_dstall), .dflush(main_1_dflush),
    .fstall(main_1_fstall), .eflush(main_1_eflush));
  Decoder decoder_1 (.instr(IF_ID_instr_out), .opcode(decoder_1_opcode), .rs1(decoder_1_rs1), .rs2(decoder_1_rs2));
  control_main main_2 (
    .opcode(decoder_1_opcode), .ALU_op(main_2_alu_op), .b_sel(main_2_b_sel), .a_sel(main_2_a_sel),
    .branch(main_2_branch), .jal(main_2_jal), .jalr(main_2_jalr), .m_wr(main_2_m_wr), .m_rd(main_2_m_rd),
    .wb_sel(main_2_wb_sel), .rf_wr(main_2_rf_wr));
  regfile_main main_3 (
    .wd(rf_mux_2_out_4), .clk(button_2_out), .we(ctrl_decoder_3_1_rf_wr), .wa(MEM_WB_out_9),
    .rd0(main_3_rd0), .rd1(main_3_rd1), .ra0(decoder_1_rs1), .ra1(decoder_1_rs2));
  ctrl_encode ctrl_encode_1 (
    .out_11(ctrl_encode_1_out_11), ._0_1(main_2_alu_op), ._8(main_2_branch), ._5_4(main_2_b_sel),
    ._10(main_2_jalr), ._7_6(main_2_a_sel), ._9(main_2_jal), ._13(main_2_m_rd), ._18(main_2_rf_wr),
    ._12(main_2_m_wr), ._16_17(main_2_wb_sel));
  Control_MUX control_mux_1 (
    .in_2(1'b0), .in_1(ctrl_encode_1_out_11), .in_3(main_1_dstall), .out_4(control_mux_1_out_4));
  ImmGen immgen_1 (.instr(IF_ID_instr_out), .Imm(immgen_1_imm));
  ID_EX ID_EX (
    .clear(main_1_eflush), .a(main_3_rd0), .pce(IF_ID_pc_out), .b(main_3_rd1), .ire(IF_ID_instr_out),
    .ctrl(control_mux_1_out_4), .Imm(immgen_1_imm), .ire_2(ID_EX_ire_2), .Imm_2(ID_EX_imm_2),
    .ctrl_2(ID_EX_ctrl_2), .pce_2(ID_EX_pce_2), .a_2(ID_EX_a_2), .b_2(ID_EX_b_2), .clk(button_2_out));  // open: hold
  ctrl_decoder ctrl_decoder_1 (
    .ctrl(ID_EX_ctrl_2), .alu_op(ctrl_decoder_1_alu_op), .branch(ctrl_decoder_1_branch),
    .jal(ctrl_decoder_1_jal), .jalr(ctrl_decoder_1_jalr), .a_sel(ctrl_decoder_1_a_sel),
    .b_sel(ctrl_decoder_1_b_sel), .m_rd(ctrl_decoder_1_m_rd));
  instr_decoder_2 instr_decoder_2_1 (
    .in_1(ID_EX_ire_2), .funct3(instr_decoder_2_1_funct3), .rd(instr_decoder_2_1_rd),
    .rs2(instr_decoder_2_1_rs2), .rs1(instr_decoder_2_1_rs1));
  or or_2 (or_2_out, ctrl_decoder_1_jal, ctrl_decoder_1_jalr);
  ADD PC_ADD_Imm (.in_1(ID_EX_pce_2), .in_2(ID_EX_imm_2), .out_3(PC_ADD_Imm_out_3));
  zero zero_1 (.in_1(A_ADD_Imm_out_3), .out_2(zero_1_out_2));
  ADD A_ADD_Imm (.in_1(ID_EX_imm_2), .in_2(ID_EX_a_2), .out_3(A_ADD_Imm_out_3));
  Forwarding_Unit forwarding_unit_1 (
    .rs1(instr_decoder_2_1_rs1), .rs2(instr_decoder_2_1_rs2), .rdw(MEM_WB_out_9), .rdm(EX_MEM_out_9),
    .rf_wr_m(ctrl_decoder_2_1_rf_wr), .rf_wr_wb(ctrl_decoder_3_1_rf_wr), .a_fwd(forwarding_unit_1_a_fwd),
    .b_fwd(forwarding_unit_1_b_fwd));
  JumpAddr jumpaddr_1 (
    .in_2(zero_1_out_2), .out_4(jumpaddr_1_out_4), .in_3(ctrl_decoder_1_jalr), .in_1(PC_ADD_Imm_out_3));
  FWD_MUX fwd_mux_1 (
    .in_1(ID_EX_a_2), .in_2(rf_mux_2_out_4), .out_5(fwd_mux_1_out_5), .in_4(forwarding_unit_1_b_fwd),
    .in_3(EX_MEM_out_8));
  FWD_MUX fwd_mux_2 (
    .in_1(ID_EX_b_2), .in_2(rf_mux_2_out_4), .out_5(fwd_mux_2_out_5), .in_4(forwarding_unit_1_a_fwd),
    .in_3(EX_MEM_out_8));
  ALU_MUX alu_mux_1 (
    .in_1(fwd_mux_1_out_5), .in_2(ID_EX_pce_2), .in_3(3'b000), .in_4(ctrl_decoder_1_a_sel),
    .out_5(alu_mux_1_out_5));
  ALU_MUX alu_mux_2 (
    .in_1(fwd_mux_2_out_5), .in_2(ID_EX_imm_2), .in_3(3'b100), .in_4(ctrl_decoder_1_b_sel),
    .out_5(alu_mux_2_out_5));
  ALU_Control alu_control_1 (.ALU_op(ctrl_decoder_1_alu_op), .instr(ID_EX_ire_2), .op(alu_control_1_op));
  Branch branch_1 (
    .ctrl_branch(ctrl_decoder_1_branch), .in0(fwd_mux_1_out_5), .in1(fwd_mux_2_out_5),
    .funct3(instr_decoder_2_1_funct3), .branch(branch_1_branch));
  alu_main main_4 (.in0(alu_mux_1_out_5), .in1(alu_mux_2_out_5), .op(alu_control_1_op), .out(main_4_out));
  EX_MEM EX_MEM (
    .in_4(instr_decoder_2_1_rd), .in_3(main_4_out), .in_1(ID_EX_ctrl_2), .in_2(fwd_mux_2_out_5),
    .out_6(EX_MEM_out_6), .out_9(EX_MEM_out_9), .out_7(EX_MEM_out_7), .out_8(EX_MEM_out_8), .clk(button_2_out));
  ctrl_decoder_2 ctrl_decoder_2_1 (
    .in_1(EX_MEM_out_6), .rf_wr(ctrl_decoder_2_1_rf_wr), .m_wr(ctrl_decoder_2_1_m_wr),
    .m_rd(ctrl_decoder_2_1_m_rd));
  data_MEM data_mem_1 (
    .in_1(EX_MEM_out_7), .out_5(data_mem_1_out_5), .in_3(ctrl_decoder_2_1_m_rd),
    .in_4(ctrl_decoder_2_1_m_wr), .in_2(EX_MEM_out_8));
  MEM_WB MEM_WB (
    .in_1(EX_MEM_out_6), .in_2(data_mem_1_out_5), .in_3(EX_MEM_out_8), .in_4(EX_MEM_out_9),
    .out_6(MEM_WB_out_6), .out_7(MEM_WB_out_7), .out_8(MEM_WB_out_8), .out_9(MEM_WB_out_9), .clk(button_2_out));
  ctrl_decoder_3 ctrl_decoder_3_1 (
    .in_1(MEM_WB_out_6), .rf_wr(ctrl_decoder_3_1_rf_wr), .wb_sel(ctrl_decoder_3_1_wb_sel));
  RF_MUX rf_mux_2 (.in_1(MEM_WB_out_8), .out_4(rf_mux_2_out_4), .in_2(MEM_WB_out_7), .in_3(ctrl_decoder_3_1_wb_sel[0]));

  // Notes on the sheet:
  //   JumpAddr
endmodule

module arrows (
  input  [1:0] in_1,
  input  [1:0] in_2,
  input  [1:0] in_3,
  input  [1:0] in_4,
  input  [1:0] in_5,
  input  [1:0] in_6,
  input  [1:0] in_7,
  input  [1:0] in_8,
  input  [1:0] in_9,
  input  [1:0] in_10,
  input  [1:0] in_11,
  input  [1:0] in_12
);
endmodule

module RegFile (
  input  [31:0] wd,
  input  clk,
  input  we,
  input  [4:0] wa,
  input  [4:0] ra0,
  input  [4:0] ra1,
  output [31:0] rd0,
  output [31:0] rd1
);

  wire and_1_out, and_2_out, equal_1_out_3, equal_2_out_3;
  wire [31:0] multiplexer_1_out, multiplexer_2_out, reg_1_out, reg_2_out, reg_3_out, reg_4_out, reg_5_out,
       reg_6_out, reg_7_out, reg_8_out, reg_9_out, reg_10_out, reg_11_out, reg_12_out, reg_13_out,
       reg_14_out, reg_15_out, reg_16_out, reg_17_out, reg_18_out, reg_19_out, reg_20_out, reg_21_out,
       reg_22_out, reg_23_out, reg_24_out, reg_25_out, reg_26_out, reg_27_out, reg_28_out, reg_29_out,
       reg_30_out, reg_31_out;

  REG reg_1 (.wd(wd), .en(we), .wa(5'b00110), .num(wa), .clk(clk), .out(reg_1_out));
  REG reg_2 (.wd(wd), .en(we), .wa(5'b01100), .num(wa), .clk(clk), .out(reg_2_out));
  REG reg_3 (.wd(wd), .en(we), .wa(5'b10010), .num(wa), .clk(clk), .out(reg_3_out));
  REG reg_4 (.wd(wd), .en(we), .wa(5'b11000), .num(wa), .clk(clk), .out(reg_4_out));
  REG reg_5 (.wd(wd), .en(we), .wa(5'b11110), .num(wa), .clk(clk), .out(reg_5_out));
  REG reg_6 (.wd(wd), .en(we), .wa({5{1'b1}}), .num(wa), .clk(clk), .out(reg_6_out));
  REG reg_7 (.wd(wd), .en(we), .wa(5'b00101), .num(wa), .clk(clk), .out(reg_7_out));
  REG reg_8 (.wd(wd), .en(we), .wa(5'b01011), .num(wa), .clk(clk), .out(reg_8_out));
  REG reg_9 (.wd(wd), .en(we), .wa(5'b10001), .num(wa), .clk(clk), .out(reg_9_out));
  REG reg_10 (.wd(wd), .en(we), .wa(5'b10111), .num(wa), .clk(clk), .out(reg_10_out));
  REG reg_11 (.wd(wd), .en(we), .wa(5'b11101), .num(wa), .clk(clk), .out(reg_11_out));
  REG reg_12 (.wd(wd), .en(we), .wa(5'b00100), .num(wa), .clk(clk), .out(reg_12_out));
  REG reg_13 (.wd(wd), .en(we), .wa(5'b01010), .num(wa), .clk(clk), .out(reg_13_out));
  REG reg_14 (.wd(wd), .en(we), .wa(5'b10000), .num(wa), .clk(clk), .out(reg_14_out));
  REG reg_15 (.wd(wd), .en(we), .wa(5'b10110), .num(wa), .clk(clk), .out(reg_15_out));
  REG reg_16 (.wd(wd), .en(we), .wa(5'b11100), .num(wa), .clk(clk), .out(reg_16_out));
  REG reg_17 (.wd(wd), .en(we), .wa(5'b00011), .num(wa), .clk(clk), .out(reg_17_out));
  REG reg_18 (.wd(wd), .en(we), .wa(5'b01001), .num(wa), .clk(clk), .out(reg_18_out));
  REG reg_19 (.wd(wd), .en(we), .wa(5'b01111), .num(wa), .clk(clk), .out(reg_19_out));
  REG reg_20 (.wd(wd), .en(we), .wa(5'b10101), .num(wa), .clk(clk), .out(reg_20_out));
  REG reg_21 (.wd(wd), .en(we), .wa(5'b11011), .num(wa), .clk(clk), .out(reg_21_out));
  REG reg_22 (.wd(wd), .en(we), .wa(5'b00010), .num(wa), .clk(clk), .out(reg_22_out));
  REG reg_23 (.wd(wd), .en(we), .wa(5'b01000), .num(wa), .clk(clk), .out(reg_23_out));
  REG reg_24 (.wd(wd), .en(we), .wa(5'b01110), .num(wa), .clk(clk), .out(reg_24_out));
  REG reg_25 (.wd(wd), .en(we), .wa(5'b10100), .num(wa), .clk(clk), .out(reg_25_out));
  REG reg_26 (.wd(wd), .en(we), .wa(5'b11010), .num(wa), .clk(clk), .out(reg_26_out));
  REG reg_27 (.wd(wd), .en(we), .wa(5'b00001), .num(wa), .clk(clk), .out(reg_27_out));
  REG reg_28 (.wd(wd), .en(we), .wa(5'b00111), .num(wa), .clk(clk), .out(reg_28_out));
  REG reg_29 (.wd(wd), .en(we), .wa(5'b01101), .num(wa), .clk(clk), .out(reg_29_out));
  REG reg_30 (.wd(wd), .en(we), .wa(5'b10011), .num(wa), .clk(clk), .out(reg_30_out));
  REG reg_31 (.wd(wd), .en(we), .wa(5'b11001), .num(wa), .clk(clk), .out(reg_31_out));
  Multiplexer #(.select(5), .width(32)) multiplexer_1 (
    .in0({32{1'b0}}), .in1(reg_27_out), .in2(reg_22_out), .in3(reg_17_out), .in4(reg_12_out),
    .in5(reg_7_out), .in6(reg_1_out), .in7(reg_28_out), .in8(reg_23_out), .in9(reg_18_out),
    .in10(reg_13_out), .in11(reg_8_out), .in12(reg_2_out), .in13(reg_29_out), .in14(reg_24_out),
    .in15(reg_19_out), .in16(reg_14_out), .in17(reg_9_out), .in18(reg_3_out), .in19(reg_30_out),
    .in20(reg_25_out), .in21(reg_20_out), .in22(reg_15_out), .in23(reg_10_out), .in24(reg_4_out),
    .in25(reg_31_out), .in26(reg_26_out), .in27(reg_21_out), .in28(reg_16_out), .in29(reg_11_out),
    .in30(reg_5_out), .in31(reg_6_out), .out(multiplexer_1_out), .sel(ra0));  // open: en
  Multiplexer #(.select(5), .width(32)) multiplexer_2 (
    .in0({32{1'b0}}), .in1(reg_27_out), .in2(reg_22_out), .in3(reg_17_out), .in4(reg_12_out),
    .in5(reg_7_out), .in6(reg_1_out), .in7(reg_28_out), .in8(reg_23_out), .in9(reg_18_out),
    .in10(reg_13_out), .in11(reg_8_out), .in12(reg_2_out), .in13(reg_29_out), .in14(reg_24_out),
    .in15(reg_19_out), .in16(reg_14_out), .in17(reg_9_out), .in18(reg_3_out), .in19(reg_30_out),
    .in20(reg_25_out), .in21(reg_20_out), .in22(reg_15_out), .in23(reg_10_out), .in24(reg_4_out),
    .in25(reg_31_out), .in26(reg_26_out), .in27(reg_21_out), .in28(reg_16_out), .in29(reg_11_out),
    .in30(reg_5_out), .in31(reg_6_out), .out(multiplexer_2_out), .sel(ra1));  // open: en
  equal equal_1 (.in_1(ra0), .in_2(wa), .out_3(equal_1_out_3));
  and and_1 (and_1_out, equal_1_out_3, we);
  equal equal_2 (.in_1(ra1), .in_2(wa), .out_3(equal_2_out_3));
  and and_2 (and_2_out, equal_2_out_3, we);
  Multiplexer #(.width(32)) multiplexer_3 (.in0(multiplexer_1_out), .in1(wd), .out(rd0), .sel(and_1_out));  // open: en
  Multiplexer #(.width(32)) multiplexer_4 (.in0(multiplexer_2_out), .in1(wd), .out(rd1), .sel(and_2_out));  // open: en
endmodule

module REG (
  input  [31:0] wd,
  input  en,
  input  [4:0] wa,
  input  [4:0] num,
  input  clk,
  output [31:0] out
);

  wire equal_1_out_3, multiplexer_1_out;

  equal equal_1 (.in_1(wa), .in_2(num), .out_3(equal_1_out_3));
  Register #(.width(32)) register_1 (.D(wd), .en(multiplexer_1_out), .Q(out), .clk(clk));  // open: clr
  Multiplexer multiplexer_1 (.in0(equal_1_out_3), .in1(1'b0), .out(multiplexer_1_out), .sel(en));  // open: en
endmodule

module equal (
  input  [4:0] in_1,
  input  [4:0] in_2,
  output out_3
);

  Comparator #(.width(5)) comparator_1 (.a(in_1), .b(in_2), .eq(out_3));  // open: gt, lt
endmodule

module ImmGen (
  input  [31:0] instr,
  output [31:0] Imm
);

  wire [11:0] multiplexer_4_out;
  wire [19:0] multiplexer_1_out, multiplexer_2_out, multiplexer_3_out;
  wire [31:0] multiplexer_5_out, multiplexer_6_out, multiplexer_7_out, multiplexer_8_out, shifter_1_out,
       shifter_2_out;

  Multiplexer #(.width(20)) multiplexer_1 (
    .in0({20{1'b0}}), .in1({20{1'b1}}), .out(multiplexer_1_out), .sel(instr[31]));  // open: en
  Multiplexer #(.width(20)) multiplexer_2 (
    .in0({20{1'b0}}), .in1({20{1'b1}}), .out(multiplexer_2_out), .sel(instr[31]));  // open: en
  Multiplexer #(.width(20)) multiplexer_3 (
    .in0({20{1'b0}}), .in1({20{1'b1}}), .out(multiplexer_3_out), .sel(instr[31]));  // open: en
  Multiplexer #(.width(12)) multiplexer_4 (
    .in0({12{1'b0}}), .in1({12{1'b1}}), .out(multiplexer_4_out), .sel(instr[31]));  // open: en
  Shifter #(.width(32)) shifter_1 (.in({multiplexer_1_out, instr[31:20]}), .\dist (5'b00001), .out(shifter_1_out));
  Shifter #(.width(32)) shifter_2 (
    .in({multiplexer_4_out, instr[31], instr[19:12], instr[20], instr[30:21]}), .\dist (5'b00001),
    .out(shifter_2_out));
  Multiplexer #(.width(32)) multiplexer_5 (
    .in0({multiplexer_1_out, instr[31:20]}), .in1(shifter_1_out), .out(multiplexer_5_out), .sel(instr[6]));  // open: en
  Multiplexer #(.width(32)) multiplexer_6 (
    .in0({multiplexer_2_out, instr[31:25], instr[11:7]}),
    .in1({multiplexer_3_out, instr[31], instr[7], instr[30:25], instr[11:8]}), .out(multiplexer_6_out),
    .sel(instr[6]));  // open: en
  Multiplexer #(.width(32)) multiplexer_7 (
    .in0({{12{1'b0}}, instr[31:12]}), .in1(shifter_2_out), .out(multiplexer_7_out), .sel(instr[6]));  // open: en
  Multiplexer #(.select(4), .width(32)) multiplexer_8 (
    .in0(multiplexer_5_out), .in1({32{1'b0}}), .in2({32{1'b0}}), .in3({32{1'b0}}), .in4(multiplexer_5_out),
    .in5(multiplexer_7_out), .in6({32{1'b0}}), .in7({32{1'b0}}), .in8(multiplexer_6_out),
    .in9(multiplexer_5_out), .in10({32{1'b0}}), .in11(multiplexer_7_out), .in12({32{1'b0}}),
    .in13(multiplexer_7_out), .in14({32{1'b0}}), .in15({32{1'b0}}), .out(multiplexer_8_out), .sel(instr[5:2]));  // open: en
  Multiplexer #(.select(2), .width(32)) multiplexer_9 (
    .in0({32{1'b0}}), .in1({32{1'b0}}), .in2({32{1'b0}}), .in3(multiplexer_8_out), .out(Imm), .sel(instr[1:0]));  // open: en

  // Notes on the sheet:
  //   sw
  //   branch
  //   lui, auipc
  //   addi, lw
  //   jalr
  //   jal
  //   opcode[6]
  //   opcode[2:5]
  //   opcode[0:1]
endmodule

module ALU (
  input  [31:0] in0,
  input  [31:0] in1,
  input  [2:0] op,
  output [31:0] out
);

  wire [31:0] adder_1_out, and_1_out, or_1_out, subtractor_1_out;

  assign and_1_out = in0 & in1;  // AND_Gate and_1, 32 bits wide
  assign or_1_out = in1 | in0;  // OR_Gate or_1, 32 bits wide
  Adder #(.width(32)) adder_1 (.a(in1), .b(in0), .out(adder_1_out));  // open: cin, cout
  Subtractor #(.width(32)) subtractor_1 (.a(in0), .b(in1), .out(subtractor_1_out));  // open: bin, bout
  Multiplexer #(.select(3), .width(32)) multiplexer_1 (
    .in0(and_1_out), .in1(or_1_out), .in2(adder_1_out), .in6(subtractor_1_out), .out(out), .sel(op));  // open: in3, in4, in5, in7, en
endmodule

module Branch (
  input  ctrl_branch,
  input  [31:0] in0,
  input  [31:0] in1,
  input  [2:0] funct3,
  output branch
);

  wire comparator_1_eq, comparator_1_lt, multiplexer_1_out, not_1_out, not_2_out;

  Comparator #(.width(32)) comparator_1 (.a(in0), .b(in1), .eq(comparator_1_eq), .lt(comparator_1_lt));  // open: gt
  not not_1 (not_1_out, comparator_1_eq);
  not not_2 (not_2_out, comparator_1_lt);
  Multiplexer #(.select(3)) multiplexer_1 (
    .in0(comparator_1_eq), .in1(not_1_out), .in2(1'b0), .in3(1'b0), .in4(comparator_1_lt), .in5(not_2_out),
    .in6(1'b0), .in7(1'b0), .out(multiplexer_1_out), .sel(funct3));  // open: en
  and and_1 (branch, ctrl_branch, multiplexer_1_out);
endmodule

module Forwarding_Unit (
  input  [4:0] rs1,
  input  [4:0] rs2,
  input  [4:0] rdw,
  input  rf_wr_wb,
  input  [4:0] rdm,
  input  rf_wr_m,
  output [1:0] b_fwd,
  output [1:0] a_fwd
);

  wire comparator_1_eq, comparator_2_eq, comparator_3_eq, comparator_4_eq, comparator_5_eq, comparator_6_eq,
       not_1_out, not_2_out;
  wire [1:0] and_2_out, and_3_out;

  Comparator #(.width(5)) comparator_1 (.a(rs1), .b(rdw), .eq(comparator_1_eq));  // open: gt, lt
  Comparator #(.width(5)) comparator_2 (.a(rs2), .b(rdw), .eq(comparator_2_eq));  // open: gt, lt
  not not_1 (not_1_out, comparator_3_eq);
  Comparator #(.width(5)) comparator_3 (.a(rdw), .b({5{1'b0}}), .eq(comparator_3_eq));  // open: gt, lt
  Comparator #(.width(5)) comparator_4 (.a(rs1), .b(rdm), .eq(comparator_4_eq));  // open: gt, lt
  Comparator #(.width(5)) comparator_5 (.a(rs2), .b(rdm), .eq(comparator_5_eq));  // open: gt, lt
  not not_2 (not_2_out, comparator_6_eq);
  Comparator #(.width(5)) comparator_6 (.a(rdm), .b({5{1'b0}}), .eq(comparator_6_eq));  // open: gt, lt
  and and_1 (and_2_out[1], rf_wr_m, not_2_out, comparator_5_eq);
  and and_2 (and_2_out[0], rf_wr_wb, not_1_out, comparator_2_eq);
  Multiplexer #(.select(2), .width(2)) multiplexer_1 (
    .in0(2'b00), .in1(2'b01), .in2(2'b10), .in3(2'b00), .out(b_fwd), .sel(and_2_out));  // open: en
  and and_3 (and_3_out[0], rf_wr_wb, not_1_out, comparator_1_eq);
  and and_4 (and_3_out[1], rf_wr_m, not_2_out, comparator_4_eq);
  Multiplexer #(.select(2), .width(2)) multiplexer_2 (
    .in0(2'b00), .in1(2'b01), .in2(2'b10), .in3(2'b00), .out(a_fwd), .sel(and_3_out));  // open: en
endmodule

module ALU_Control (
  input  [1:0] ALU_op,
  input  [31:0] instr,
  output [2:0] op
);

  wire [2:0] multiplexer_1_out, multiplexer_2_out, multiplexer_3_out, multiplexer_4_out;

  Multiplexer #(.width(3)) multiplexer_1 (
    .in0(3'b010), .in1(3'b110), .out(multiplexer_1_out), .sel(instr[26]));  // open: en
  Multiplexer #(.width(3)) multiplexer_2 (
    .in0(3'b001), .in1(3'b110), .out(multiplexer_2_out), .sel(instr[26]));  // open: en
  Multiplexer #(.width(3)) multiplexer_3 (
    .in0(3'b000), .in1(3'b110), .out(multiplexer_3_out), .sel(instr[26]));  // open: en
  Multiplexer #(.select(3), .width(3)) multiplexer_4 (
    .in0(multiplexer_1_out), .in6(multiplexer_2_out), .in7(multiplexer_3_out), .out(multiplexer_4_out),
    .sel(instr[14:12]));  // open: in1, in2, in3, in4, in5, en
  Multiplexer #(.select(2), .width(3)) multiplexer_5 (
    .in0(3'b010), .in1(3'b110), .in2(multiplexer_4_out), .in3(3'b110), .out(op), .sel(ALU_op));  // open: en

  // Notes on the sheet:
  //   ADD
  //   SUB
  //   funct3
  //   funct7[5]
  //   OR
  //   AND
  //   ADD
  //   SUB
endmodule

module Hazard_Unit (
  input  in_1,
  input  in_2,
  input  in_3,
  input  [4:0] in_4,
  input  [4:0] in_5,
  input  [4:0] in_6,
  output out_7,
  output out_8,
  output out_9,
  output out_10
);
endmodule

module Control (
  input  [6:0] opcode,
  output [1:0] ALU_op,
  output [1:0] b_sel,
  output [1:0] a_sel,
  output branch,
  output jal,
  output jalr,
  output m_wr,
  output m_rd,
  output [1:0] wb_sel,
  output rf_wr
);
endmodule

module PC (
  input  [31:0] in,
  input  hold,
  input  clk,
  input  clear,
  output [31:0] out
);

  wire not_1_out;

  not not_1 (not_1_out, hold);
  Register #(.width(32)) register_1 (.D(in), .en(not_1_out), .Q(out), .clk(clk), .clr(clear));
endmodule

module IF_ID (
  input  [31:0] pc_in,
  input  [31:0] instr_in,
  input  hold,
  input  clk,
  input  clear,
  output [31:0] pc_out,
  output [31:0] instr_out
);

  wire d_ff_1_q, not_1_out;

  not not_1 (not_1_out, hold);
  Register #(.width(32)) register_1 (.D(pc_in), .en(not_1_out), .Q(pc_out), .clk(clk), .clr(d_ff_1_q));
  Register #(.width(32)) register_2 (.D(instr_in), .en(not_1_out), .Q(instr_out), .clk(clk), .clr(d_ff_1_q));
  D_Flip_Flop d_ff_1 (.clk(clk), .D(clear), .Q(d_ff_1_q));  // open: Qn, preset, en, reset
endmodule

module instr_MEM (
  input  [31:0] in_1,
  input  in_2,
  output [31:0] out_3
);

  wire [31:0] divider_1_out;

  Divider #(.width(32)) divider_1 (.a(in_1), .b(32'h4), .out(divider_1_out));  // open: upper, rem
  RAM #(.dataWidth(32)) ram_1 (.addr(divider_1_out[7:0]), .data(out_3), .clk(in_2));  // open: sel, ld, clr
endmodule

module PC_ADD_4 (
  input  [31:0] in_1,
  input  [2:0] in_2,
  output [31:0] out_3
);

  Adder #(.width(32)) adder_1 (.a(in_1), .b({{29{1'b0}}, in_2}), .out(out_3));  // open: cin, cout
endmodule

module ID_EX (
  input  [31:0] pce,
  input  [31:0] a,
  input  [31:0] b,
  input  [31:0] ire,
  input  [31:0] ctrl,
  input  [31:0] Imm,
  input  hold,
  input  clk,
  input  clear,
  output [31:0] pce_2,
  output [31:0] a_2,
  output [31:0] b_2,
  output [31:0] ire_2,
  output [31:0] ctrl_2,
  output [31:0] Imm_2
);

  wire d_ff_1_q, not_1_out;

  not not_1 (not_1_out, hold);
  Register #(.width(32)) register_1 (.D(pce), .en(not_1_out), .Q(pce_2), .clk(clk), .clr(d_ff_1_q));
  Register #(.width(32)) register_2 (.D(a), .en(not_1_out), .Q(a_2), .clk(clk), .clr(d_ff_1_q));
  Register #(.width(32)) register_3 (.D(b), .en(not_1_out), .Q(b_2), .clk(clk), .clr(d_ff_1_q));
  Register #(.width(32)) register_4 (.D(ire), .en(not_1_out), .Q(ire_2), .clk(clk), .clr(d_ff_1_q));
  Register #(.width(32)) register_5 (.D(ctrl), .en(not_1_out), .Q(ctrl_2), .clk(clk), .clr(d_ff_1_q));
  Register #(.width(32)) register_6 (.D(Imm), .en(not_1_out), .Q(Imm_2), .clk(clk), .clr(d_ff_1_q));
  D_Flip_Flop d_ff_1 (.clk(clk), .D(clear), .Q(d_ff_1_q));  // open: Qn, preset, en, reset
endmodule

module Instr_MUX (
  input  [31:0] in_1,
  input  in_2,
  input  sel,
  output [31:0] out_4
);

  Multiplexer #(.width(32)) multiplexer_1 (.in0(in_1), .in1({{31{1'b0}}, in_2}), .out(out_4), .sel(sel));  // open: en
endmodule

module Decoder (
  input  [31:0] instr,
  output [6:0] opcode,
  output [4:0] rs1,
  output [4:0] rs2
);


  assign opcode = instr[6:0];
  assign rs1 = instr[19:15];
  assign rs2 = instr[24:20];
endmodule

module Control_MUX (
  input  [31:0] in_1,
  input  in_2,
  input  in_3,
  output [31:0] out_4
);

  Multiplexer #(.width(32)) multiplexer_1 (.in0(in_1), .in1({{31{1'b0}}, in_2}), .out(out_4), .sel(in_3));  // open: en
endmodule

module ctrl_decoder (
  input  [31:0] ctrl,
  output [1:0] alu_op,
  output [1:0] b_sel,
  output [1:0] a_sel,
  output branch,
  output jal,
  output jalr,
  output m_rd
);


  assign a_sel = ctrl[7:6];
  assign alu_op = ctrl[1:0];
  assign b_sel = ctrl[5:4];
  assign branch = ctrl[8];
  assign jal = ctrl[9];
  assign jalr = ctrl[10];
  assign m_rd = ctrl[13];
endmodule

module ADD (
  input  [31:0] in_1,
  input  [31:0] in_2,
  output [31:0] out_3
);

  Adder #(.width(32)) adder_1 (.a(in_1), .b(in_2), .out(out_3));  // open: cin, cout
endmodule

module instr_decoder_2 (
  input  [31:0] in_1,
  output [4:0] rd,
  output [2:0] funct3,
  output [4:0] rs1,
  output [4:0] rs2
);


  assign funct3 = in_1[14:12];
  assign rd = in_1[11:7];
  assign rs1 = in_1[19:15];
  assign rs2 = in_1[24:20];
endmodule

module FWD_MUX (
  input  [31:0] in_1,
  input  [31:0] in_2,
  input  [31:0] in_3,
  input  [1:0] in_4,
  output [31:0] out_5
);

  Multiplexer #(.select(2), .width(32)) multiplexer_1 (
    .in0(in_1), .in1(in_2), .in2(in_3), .in3({32{1'b0}}), .out(out_5), .sel(in_4));  // open: en
endmodule

module ALU_MUX (
  input  [31:0] in_1,
  input  [31:0] in_2,
  input  [2:0] in_3,
  input  [1:0] in_4,
  output [31:0] out_5
);

  Multiplexer #(.select(2), .width(32)) multiplexer_1 (
    .in0(in_1), .in1(in_2), .in2({{29{1'b0}}, in_3}), .in3({32{1'b0}}), .out(out_5), .sel(in_4));  // open: en
endmodule

module JumpAddr (
  input  [31:0] in_1,
  input  [31:0] in_2,
  input  in_3,
  output [31:0] out_4
);

  Multiplexer #(.width(32)) multiplexer_1 (.in0(in_1), .in1(in_2), .out(out_4), .sel(in_3));  // open: en
endmodule

module zero (
  input  [31:0] in_1,
  output [31:0] out_2
);

  wire [31:0] not_1_out;

  assign not_1_out = ~32'h1;  // NOT_Gate not_1, 32 bits wide
  assign out_2 = not_1_out & in_1;  // AND_Gate and_1, 32 bits wide
endmodule

module EX_MEM (
  input  [31:0] in_1,
  input  [31:0] in_2,
  input  [31:0] in_3,
  input  [4:0] in_4,
  input  clk,
  output [31:0] out_6,
  output [31:0] out_7,
  output [31:0] out_8,
  output [4:0] out_9
);

  Register #(.width(32)) register_1 (.D(in_1), .Q(out_6), .clk(clk));  // open: en, clr
  Register #(.width(32)) register_2 (.D(in_2), .Q(out_7), .clk(clk));  // open: en, clr
  Register #(.width(32)) register_3 (.D(in_3), .Q(out_8), .clk(clk));  // open: en, clr
  Register #(.width(5)) register_4 (.D(in_4), .Q(out_9), .clk(clk));  // open: en, clr
endmodule

module ctrl_decoder_2 (
  input  [31:0] in_1,
  output m_wr,
  output m_rd,
  output rf_wr
);


  assign m_rd = in_1[13];
  assign m_wr = in_1[12];
  assign rf_wr = in_1[18];
endmodule

module data_MEM (
  input  [31:0] in_1,
  input  [31:0] in_2,
  input  in_3,
  input  in_4,
  output [31:0] out_5
);
endmodule

module MEM_WB (
  input  [31:0] in_1,
  input  [31:0] in_2,
  input  [31:0] in_3,
  input  [4:0] in_4,
  input  clk,
  output [31:0] out_6,
  output [31:0] out_7,
  output [31:0] out_8,
  output [4:0] out_9
);

  Register #(.width(32)) register_1 (.D(in_1), .Q(out_6), .clk(clk));  // open: en, clr
  Register #(.width(32)) register_2 (.D(in_2), .Q(out_7), .clk(clk));  // open: en, clr
  Register #(.width(32)) register_3 (.D(in_3), .Q(out_8), .clk(clk));  // open: en, clr
  Register #(.width(5)) register_4 (.D(in_4), .Q(out_9), .clk(clk));  // open: en, clr
endmodule

module RF_MUX (
  input  [31:0] in_1,
  input  [31:0] in_2,
  input  in_3,
  output [31:0] out_4
);

  Multiplexer #(.width(32)) multiplexer_1 (.in0(in_1), .in1(in_2), .out(out_4), .sel(in_3));  // open: en
endmodule

module ctrl_decoder_3 (
  input  [31:0] in_1,
  output [1:0] wb_sel,
  output rf_wr
);


  assign rf_wr = in_1[18];
  assign wb_sel = in_1[17:16];
endmodule

module ctrl_temp (
  input  [6:0] in_1,
  output ALU_op,
  output out_3,
  output out_4,
  output out_5,
  output out_6,
  output out_7,
  output out_8,
  output out_9,
  output out_10,
  output out_11
);
endmodule

module ctrl_encode (
  input  [1:0] _0_1,
  input  [1:0] _5_4,
  input  [1:0] _7_6,
  input  _8,
  input  _9,
  input  _10,
  input  _12,
  input  _13,
  input  [1:0] _16_17,
  input  _18,
  output [31:0] out_11
);


  assign out_11 = {{13{1'b0}}, _18, _16_17, 2'b00, _13, _12, 1'b0, _10, _9, _8, _7_6, _5_4, 2'b00, _0_1};
endmodule
