// Logisim project cpu.circ as structural Verilog: 15 circuits, main circuit main
module main (
  input  in_1
);

  wire button_1_out, ctrl_decoder_1_branch, ctrl_decoder_1_jal, ctrl_decoder_1_jalr, ctrl_decoder_1_m_rd,
       ctrl_decoder_2_1_m_rd, ctrl_decoder_2_1_m_wr, ctrl_decoder_2_1_rf_wr, ctrl_decoder_3_1_rf_wr,
       main_1_dflush, main_1_dstall, main_1_eflush, main_1_fstall, main_2_branch, main_2_jal, main_2_jalr,
       main_2_m_rd, main_2_m_wr, main_2_rf_wr, main_7_p5, or_1_out, or_2_out, or_3_out, or_4_out;
  wire [1:0] ctrl_decoder_1_a_sel, ctrl_decoder_1_alu_op, ctrl_decoder_1_b_sel, ctrl_decoder_3_1_wb_sel,
       main_2_a_sel, main_2_alu_op, main_2_b_sel, main_2_wb_sel, main_5_a_fwd, main_5_b_fwd;
  wire [2:0] instr_decoder_2_1_funct3, main_6_op;
  wire [4:0] decoder_1_rs1, decoder_1_rs2, EX_MEM_out_10, instr_decoder_2_1_rd, instr_decoder_2_1_rs1,
       instr_decoder_2_1_rs2, MEM_WB_out_10;
  wire [6:0] decoder_1_opcode;
  wire [31:0] A_ADD_Imm_out_3, add_1_out_3, ctrl_encode_1_out_11, EX_MEM_out_7, EX_MEM_out_8, EX_MEM_out_9,
       ID_EX_a_2, ID_EX_b_2, ID_EX_ctrl_2, ID_EX_imm_2, ID_EX_ire_2, ID_EX_pce_2, IF_ID_instr_out,
       IF_ID_pc_out, instr_mem_1_out_3, main_3_rd0, main_3_rd1, main_4_imm, main_8_out, main_9_out,
       MEM_WB_out_7, MEM_WB_out_8, MEM_WB_out_9, mux_2_north_1_out_4, mux_2_north_2_out_4,
       mux_2_north_reverse_1_out_4, mux_2_south_reverse_1_out_4, mux_2_south_reverse_2_out_4,
       mux_3_north_1_out_5, mux_3_north_2_out_5, mux_3_south_1_out_5, mux_3_south_2_out_5, pc_1_out,
       PC_ADD_Imm_out_3, zero_1_out_2;

  MUX_2_North mux_2_north_1 (
    .in_1(add_1_out_3), .in_2(mux_2_north_2_out_4), .in_3(or_1_out), .out_4(mux_2_north_1_out_4));
  Button button_1 (.out(button_1_out));
  PC pc_1 (.in(mux_2_north_1_out_4), .clear(in_1), .hold(main_1_fstall), .out(pc_1_out), .clk(button_1_out));
  ADD add_1 (.in_1(32'h4), .in_2(pc_1_out), .out_3(add_1_out_3));
  instr_MEM instr_mem_1 (.in_1(pc_1_out), .out_3(instr_mem_1_out_3), .in_2(button_1_out));
  or or_1 (or_1_out, main_7_p5, or_4_out);
  MUX_2_South_reverse mux_2_south_reverse_1 (
    .in_1(instr_mem_1_out_3), .in_2({32{1'b0}}), .in_3(main_1_dflush), .out_4(mux_2_south_reverse_1_out_4));
  IF_ID IF_ID (
    .pc_in(pc_1_out), .instr_in(mux_2_south_reverse_1_out_4), .hold(main_1_dstall), .clear(or_2_out),
    .pc_out(IF_ID_pc_out), .instr_out(IF_ID_instr_out), .clk(button_1_out));
  or or_2 (or_2_out, in_1, main_1_dflush);
  hazardunit_main main_1 (
    .branch(main_7_p5), .m_rd_e(ctrl_decoder_1_m_rd), .jump(or_4_out), .rs1(decoder_1_rs1),
    .rs2(decoder_1_rs2), .rde(instr_decoder_2_1_rd), .dstall(main_1_dstall), .dflush(main_1_dflush),
    .fstall(main_1_fstall), .eflush(main_1_eflush));
  Decoder decoder_1 (.instr(IF_ID_instr_out), .opcode(decoder_1_opcode), .rs1(decoder_1_rs1), .rs2(decoder_1_rs2));
  control_main main_2 (
    .opcode(decoder_1_opcode), .ALU_op(main_2_alu_op), .b_sel(main_2_b_sel), .a_sel(main_2_a_sel),
    .branch(main_2_branch), .jal(main_2_jal), .jalr(main_2_jalr), .m_wr(main_2_m_wr), .m_rd(main_2_m_rd),
    .wb_sel(main_2_wb_sel), .rf_wr(main_2_rf_wr));
  regfile_main main_3 (
    .wd(mux_2_north_reverse_1_out_4), .clk(button_1_out), .we(ctrl_decoder_3_1_rf_wr), .wa(MEM_WB_out_10),
    .rd1(main_3_rd1), .ra1(decoder_1_rs2), .ra0(decoder_1_rs1), .rd0(main_3_rd0), .clear(in_1));  // open: rd2, ra2
  ctrl_encode ctrl_encode_1 (
    .out_11(ctrl_encode_1_out_11), ._0_1(main_2_alu_op), ._8(main_2_branch), ._5_4(main_2_b_sel),
    ._10(main_2_jalr), ._7_6(main_2_a_sel), ._9(main_2_jal), ._13(main_2_m_rd), ._18(main_2_rf_wr),
    ._12(main_2_m_wr), ._16_17(main_2_wb_sel));
  imm_gen_main main_4 (.instr(IF_ID_instr_out), .Imm(main_4_imm));
  MUX_2_South_reverse mux_2_south_reverse_2 (
    .in_1(ctrl_encode_1_out_11), .in_2({32{1'b0}}), .in_3(main_1_dstall), .out_4(mux_2_south_reverse_2_out_4));
  or or_3 (or_3_out, main_1_eflush, in_1);
  ID_EX ID_EX (
    .clear(or_3_out), .a(main_3_rd0), .pce(IF_ID_pc_out), .b(main_3_rd1), .ire(IF_ID_instr_out),
    .ctrl(mux_2_south_reverse_2_out_4), .Imm(main_4_imm), .ire_2(ID_EX_ire_2), .Imm_2(ID_EX_imm_2),
    .ctrl_2(ID_EX_ctrl_2), .pce_2(ID_EX_pce_2), .a_2(ID_EX_a_2), .b_2(ID_EX_b_2), .clk(button_1_out));  // open: hold
  ctrl_decoder ctrl_decoder_1 (
    .ctrl(ID_EX_ctrl_2), .alu_op(ctrl_decoder_1_alu_op), .branch(ctrl_decoder_1_branch),
    .jal(ctrl_decoder_1_jal), .jalr(ctrl_decoder_1_jalr), .a_sel(ctrl_decoder_1_a_sel),
    .b_sel(ctrl_decoder_1_b_sel), .m_rd(ctrl_decoder_1_m_rd));
  instr_decoder_2 instr_decoder_2_1 (
    .in_1(ID_EX_ire_2), .funct3(instr_decoder_2_1_funct3), .rd(instr_decoder_2_1_rd),
    .rs2(instr_decoder_2_1_rs2), .rs1(instr_decoder_2_1_rs1));
  or or_4 (or_4_out, ctrl_decoder_1_jal, ctrl_decoder_1_jalr);
  ADD PC_ADD_Imm (.in_1(ID_EX_pce_2), .in_2(ID_EX_imm_2), .out_3(PC_ADD_Imm_out_3));
  zero zero_1 (.in_1(A_ADD_Imm_out_3), .out_2(zero_1_out_2));
  ADD A_ADD_Imm (.in_1(ID_EX_imm_2), .in_2(ID_EX_a_2), .out_3(A_ADD_Imm_out_3));
  forwarding_unit_main main_5 (
    .rs1(instr_decoder_2_1_rs1), .rs2(instr_decoder_2_1_rs2), .rdw(MEM_WB_out_10),
    .rf_wr_wb(ctrl_decoder_3_1_rf_wr), .rdm(EX_MEM_out_10), .rf_wr_m(ctrl_decoder_2_1_rf_wr),
    .b_fwd(main_5_b_fwd), .a_fwd(main_5_a_fwd));
  MUX_2_North mux_2_north_2 (
    .in_1(PC_ADD_Imm_out_3), .in_2(zero_1_out_2), .in_3(ctrl_decoder_1_jalr), .out_4(mux_2_north_2_out_4));
  MUX_3_South mux_3_south_1 (
    .in_1(ID_EX_a_2), .in_2(mux_2_north_reverse_1_out_4), .in_3(EX_MEM_out_9), .in_4(main_5_a_fwd),
    .out_5(mux_3_south_1_out_5));
  MUX_3_South mux_3_south_2 (
    .in_1(ID_EX_b_2), .in_2(mux_2_north_reverse_1_out_4), .in_3(EX_MEM_out_9), .in_4(main_5_b_fwd),
    .out_5(mux_3_south_2_out_5));
  MUX_3_North mux_3_north_1 (
    .in_1(mux_3_south_1_out_5), .in_2(ID_EX_pce_2), .in_3({32{1'b0}}), .in_4(ctrl_decoder_1_a_sel),
    .out_5(mux_3_north_1_out_5));
  MUX_3_North mux_3_north_2 (
    .in_1(mux_3_south_2_out_5), .in_2(ID_EX_imm_2), .in_3(32'h4), .in_4(ctrl_decoder_1_b_sel),
    .out_5(mux_3_north_2_out_5));
  alu_control_main main_6 (.ALU_op(ctrl_decoder_1_alu_op), .instr(ID_EX_ire_2), .op(main_6_op));
  // branch_main main_7: pin names not known; wires that end beside it: mux_3_south_1_out_5, instr_decoder_2_1_funct3, mux_3_south_2_out_5, ctrl_decoder_1_branch, main_7_p5
  alu_main main_8 (.in0(mux_3_north_1_out_5), .in1(mux_3_north_2_out_5), .op(main_6_op), .out(main_8_out));
  EX_MEM EX_MEM (
    .in_4(instr_decoder_2_1_rd), .in_3(main_8_out), .in_1(ID_EX_ctrl_2), .in_2(mux_3_south_2_out_5),
    .out_7(EX_MEM_out_7), .out_10(EX_MEM_out_10), .out_8(EX_MEM_out_8), .out_9(EX_MEM_out_9),
    .clk(button_1_out), .clear(in_1));
  ctrl_decoder_2 ctrl_decoder_2_1 (
    .in_1(EX_MEM_out_7), .rf_wr(ctrl_decoder_2_1_rf_wr), .m_wr(ctrl_decoder_2_1_m_wr),
    .m_rd(ctrl_decoder_2_1_m_rd));
  data_memory_main main_9 (
    .wd(EX_MEM_out_8), .wa(EX_MEM_out_9), .m_rd(ctrl_decoder_2_1_m_rd), .m_wr(ctrl_decoder_2_1_m_wr),
    .out(main_9_out), .clk(button_1_out));
  MEM_WB MEM_WB (
    .in_1(EX_MEM_out_7), .in_2(main_9_out), .in_3(EX_MEM_out_9), .in_4(EX_MEM_out_10), .out_7(MEM_WB_out_7),
    .out_8(MEM_WB_out_8), .out_9(MEM_WB_out_9), .out_10(MEM_WB_out_10), .clk(button_1_out), .clear(in_1));
  ctrl_decoder_3 ctrl_decoder_3_1 (
    .in_1(MEM_WB_out_7), .rf_wr(ctrl_decoder_3_1_rf_wr), .wb_sel(ctrl_decoder_3_1_wb_sel));
  MUX_2_North_reverse mux_2_north_reverse_1 (
    .in_1(MEM_WB_out_9), .in_2(MEM_WB_out_8), .in_3(ctrl_decoder_3_1_wb_sel[0]),
    .out_4(mux_2_north_reverse_1_out_4));

  // Notes on the sheet:
  //   JumpAddr
endmodule

module PC (
  input  [31:0] in,
  input  hold,
  input  clk,
  input  clear,
  output [31:0] out
);

  wire not_1_out;

  not not_1 (not_1_out, hold);
  Register #(.width(32)) register_1 (.D(in), .en(not_1_out), .Q(out), .clk(clk), .clr(clear));
endmodule

module IF_ID (
  input  [31:0] pc_in,
  input  [31:0] instr_in,
  input  hold,
  input  clk,
  input  clear,
  output [31:0] pc_out,
  output [31:0] instr_out
);

  wire d_ff_1_q, not_1_out;

  not not_1 (not_1_out, hold);
  Register #(.width(32)) register_1 (.D(pc_in), .en(not_1_out), .Q(pc_out), .clk(clk), .clr(d_ff_1_q));
  Register #(.width(32)) register_2 (.D(instr_in), .en(not_1_out), .Q(instr_out), .clk(clk), .clr(d_ff_1_q));
  D_Flip_Flop d_ff_1 (.clk(clk), .D(clear), .Q(d_ff_1_q));  // open: Qn, preset, en, reset
endmodule

module instr_MEM (
  input  [31:0] in_1,
  input  in_2,
  output [31:0] out_3
);

  wire [7:0] bitselector_1_out;
  wire [31:0] divider_1_out;

  Divider #(.width(32)) divider_1 (.a(in_1), .b(32'h4), .out(divider_1_out));  // open: upper, rem
  BitSelector #(.width(32), .group(8)) bitselector_1 (.in(divider_1_out), .out(bitselector_1_out), .sel(2'b00));
  RAM #(.dataWidth(32)) ram_1 (.addr(bitselector_1_out), .data(out_3), .clk(in_2));  // open: sel, ld, clr
endmodule

module ID_EX (
  input  [31:0] pce,
  input  [31:0] a,
  input  [31:0] b,
  input  [31:0] ire,
  input  [31:0] ctrl,
  input  [31:0] Imm,
  input  hold,
  input  clk,
  input  clear,
  output [31:0] pce_2,
  output [31:0] a_2,
  output [31:0] b_2,
  output [31:0] ire_2,
  output [31:0] ctrl_2,
  output [31:0] Imm_2
);

  wire d_ff_1_q, not_1_out;

  not not_1 (not_1_out, hold);
  Register #(.width(32)) register_1 (.D(pce), .en(not_1_out), .Q(pce_2), .clk(clk), .clr(d_ff_1_q));
  Register #(.width(32)) register_2 (.D(a), .en(not_1_out), .Q(a_2), .clk(clk), .clr(d_ff_1_q));
  Register #(.width(32)) register_3 (.D(b), .en(not_1_out), .Q(b_2), .clk(clk), .clr(d_ff_1_q));
  Register #(.width(32)) register_4 (.D(ire), .en(not_1_out), .Q(ire_2), .clk(clk), .clr(d_ff_1_q));
  Register #(.width(32)) register_5 (.D(ctrl), .en(not_1_out), .Q(ctrl_2), .clk(clk), .clr(d_ff_1_q));
  Register #(.width(32)) register_6 (.D(Imm), .en(not_1_out), .Q(Imm_2), .clk(clk), .clr(d_ff_1_q));
  D_Flip_Flop d_ff_1 (.clk(clk), .D(clear), .Q(d_ff_1_q));  // open: Qn, preset, en, reset
endmodule

module Decoder (
  input  [31:0] instr,
  output [6:0] opcode,
  output [4:0] rs1,
  output [4:0] rs2
);


  assign opcode = instr[6:0];
  assign rs1 = instr[19:15];
  assign rs2 = instr[24:20];
endmodule

module ctrl_decoder (
  input  [31:0] ctrl,
  output [1:0] alu_op,
  output [1:0] b_sel,
  output [1:0] a_sel,
  output branch,
  output jal,
  output jalr,
  output m_rd
);


  assign a_sel = ctrl[7:6];
  assign alu_op = ctrl[1:0];
  assign b_sel = ctrl[5:4];
  assign branch = ctrl[8];
  assign jal = ctrl[9];
  assign jalr = ctrl[10];
  assign m_rd = ctrl[13];
endmodule

module ADD (
  input  [31:0] in_1,
  input  [31:0] in_2,
  output [31:0] out_3
);

  Adder #(.width(32)) adder_1 (.a(in_1), .b(in_2), .out(out_3));  // open: cin, cout
endmodule

module instr_decoder_2 (
  input  [31:0] in_1,
  output [4:0] rd,
  output [2:0] funct3,
  output [4:0] rs1,
  output [4:0] rs2
);


  assign funct3 = in_1[14:12];
  assign rd = in_1[11:7];
  assign rs1 = in_1[19:15];
  assign rs2 = in_1[24:20];
endmodule

module zero (
  input  [31:0] in_1,
  output [31:0] out_2
);

  wire [31:0] not_1_out;

  assign not_1_out = ~32'h1;  // NOT_Gate not_1, 32 bits wide
  assign out_2 = not_1_out & in_1;  // AND_Gate and_1, 32 bits wide
endmodule

module EX_MEM (
  input  [31:0] in_1,
  input  [31:0] in_2,
  input  [31:0] in_3,
  input  [4:0] in_4,
  input  clk,
  input  clear,
  output [31:0] out_7,
  output [31:0] out_8,
  output [31:0] out_9,
  output [4:0] out_10
);

  Register #(.width(32)) register_1 (.D(in_1), .Q(out_7), .clk(clk), .clr(clear));  // open: en
  Register #(.width(32)) register_2 (.D(in_2), .Q(out_8), .clk(clk), .clr(clear));  // open: en
  Register #(.width(32)) register_3 (.D(in_3), .Q(out_9), .clk(clk), .clr(clear));  // open: en
  Register #(.width(5)) register_4 (.D(in_4), .Q(out_10), .clk(clk), .clr(clear));  // open: en
endmodule

module ctrl_decoder_2 (
  input  [31:0] in_1,
  output m_wr,
  output m_rd,
  output rf_wr
);


  assign m_rd = in_1[13];
  assign m_wr = in_1[12];
  assign rf_wr = in_1[18];
endmodule

module MEM_WB (
  input  [31:0] in_1,
  input  [31:0] in_2,
  input  [31:0] in_3,
  input  [4:0] in_4,
  input  clk,
  input  clear,
  output [31:0] out_7,
  output [31:0] out_8,
  output [31:0] out_9,
  output [4:0] out_10
);

  Register #(.width(32)) register_1 (.D(in_1), .Q(out_7), .clk(clk), .clr(clear));  // open: en
  Register #(.width(32)) register_2 (.D(in_2), .Q(out_8), .clk(clk), .clr(clear));  // open: en
  Register #(.width(32)) register_3 (.D(in_3), .Q(out_9), .clk(clk), .clr(clear));  // open: en
  Register #(.width(5)) register_4 (.D(in_4), .Q(out_10), .clk(clk), .clr(clear));  // open: en
endmodule

module ctrl_decoder_3 (
  input  [31:0] in_1,
  output [1:0] wb_sel,
  output rf_wr
);


  assign rf_wr = in_1[18];
  assign wb_sel = in_1[17:16];
endmodule

module ctrl_encode (
  input  [1:0] _0_1,
  input  [1:0] _5_4,
  input  [1:0] _7_6,
  input  _8,
  input  _9,
  input  _10,
  input  _12,
  input  _13,
  input  [1:0] _16_17,
  input  _18,
  output [31:0] out_11
);


  assign out_11 = {{13{1'b0}}, _18, _16_17, 2'b00, _13, _12, 1'b0, _10, _9, _8, _7_6, _5_4, 2'b00, _0_1};
endmodule
