// Logisim project forwarding_unit.circ as structural Verilog: 1 circuit, main circuit main
module main (
  input  [4:0] rs1,
  input  [4:0] rs2,
  input  [4:0] rdw,
  input  rf_wr_wb,
  input  [4:0] rdm,
  input  rf_wr_m,
  output [1:0] b_fwd,
  output [1:0] a_fwd
);

  wire comparator_1_eq, comparator_2_eq, comparator_3_eq, comparator_4_eq, comparator_5_eq, comparator_6_eq,
       not_1_out, not_2_out;
  wire [1:0] and_1_out, and_4_out;

  Comparator #(.width(5)) comparator_1 (.a(rs1), .b(rdw), .eq(comparator_1_eq));  // open: gt, lt
  Comparator #(.width(5)) comparator_2 (.a(rs2), .b(rdw), .eq(comparator_2_eq));  // open: gt, lt
  Comparator #(.width(5)) comparator_3 (.a(rdw), .b({5{1'b0}}), .eq(comparator_3_eq));  // open: gt, lt
  Comparator #(.width(5)) comparator_4 (.a(rs1), .b(rdm), .eq(comparator_4_eq));  // open: gt, lt
  Comparator #(.width(5)) comparator_5 (.a(rs2), .b(rdm), .eq(comparator_5_eq));  // open: gt, lt
  Comparator #(.width(5)) comparator_6 (.a(rdm), .b({5{1'b0}}), .eq(comparator_6_eq));  // open: gt, lt
  not not_1 (not_1_out, comparator_3_eq);
  not not_2 (not_2_out, comparator_6_eq);
  and and_1 (and_1_out[0], rf_wr_wb, not_1_out, comparator_2_eq);
  and and_2 (and_1_out[1], rf_wr_m, not_2_out, comparator_5_eq);
  Multiplexer #(.select(2), .width(2)) multiplexer_1 (
    .in0(2'b00), .in1(2'b01), .in2(2'b10), .in3(2'b00), .out(b_fwd), .sel(and_1_out));  // open: en
  and and_3 (and_4_out[1], rf_wr_m, not_2_out, comparator_4_eq);
  and and_4 (and_4_out[0], rf_wr_wb, not_1_out, comparator_1_eq);
  Multiplexer #(.select(2), .width(2)) multiplexer_2 (
    .in0(2'b00), .in1(2'b01), .in2(2'b10), .in3(2'b00), .out(a_fwd), .sel(and_4_out));  // open: en
endmodule
