// Logisim project imm_gen.circ as structural Verilog: 1 circuit, main circuit main
module main (
  input  [31:0] instr,
  output [31:0] Imm
);

  wire [31:0] bit_extender_1_out, bit_extender_2_out, bit_extender_3_out, bit_extender_4_out,
       bit_extender_5_out, multiplexer_1_out, multiplexer_2_out, multiplexer_3_out, multiplexer_4_out,
       shifter_1_out, shifter_2_out, shifter_3_out;

  assign bit_extender_1_out = {{20{instr[31]}}, instr[31:20]};  // Bit_Extender bit_extender_1
  assign bit_extender_2_out = {{20{instr[31]}}, {instr[31:25], instr[11:7]}};  // Bit_Extender bit_extender_2
  assign bit_extender_3_out = {{20{instr[31]}}, {instr[31], instr[7], instr[30:25], instr[11:8]}};  // Bit_Extender bit_extender_3
  assign bit_extender_4_out = {{12{1'b0}}, instr[31:12]};  // Bit_Extender bit_extender_4
  assign bit_extender_5_out = {{12{instr[31]}}, {instr[31], instr[19:12], instr[20], instr[30:21]}};  // Bit_Extender bit_extender_5
  Shifter #(.width(32)) shifter_1 (.in(bit_extender_1_out), .\dist (5'b00001), .out(shifter_1_out));
  Shifter #(.width(32)) shifter_2 (.in(bit_extender_4_out), .\dist (5'b01100), .out(shifter_2_out));
  Shifter #(.width(32)) shifter_3 (.in(bit_extender_5_out), .\dist (5'b00001), .out(shifter_3_out));
  Multiplexer #(.width(32)) multiplexer_1 (
    .in0(bit_extender_1_out), .in1(shifter_1_out), .out(multiplexer_1_out), .sel(instr[6]));  // open: en
  Multiplexer #(.width(32)) multiplexer_2 (
    .in0(bit_extender_2_out), .in1(bit_extender_3_out), .out(multiplexer_2_out), .sel(instr[6]));  // open: en
  Multiplexer #(.width(32)) multiplexer_3 (
    .in0(shifter_2_out), .in1(shifter_3_out), .out(multiplexer_3_out), .sel(instr[6]));  // open: en
  Multiplexer #(.select(4), .width(32)) multiplexer_4 (
    .in0(multiplexer_1_out), .in1({32{1'b0}}), .in2({32{1'b0}}), .in3({32{1'b0}}), .in4(multiplexer_1_out),
    .in5(multiplexer_3_out), .in6({32{1'b0}}), .in7({32{1'b0}}), .in8(multiplexer_2_out),
    .in9(multiplexer_1_out), .in10({32{1'b0}}), .in11(multiplexer_3_out), .in12({32{1'b0}}),
    .in13(multiplexer_3_out), .in14({32{1'b0}}), .in15({32{1'b0}}), .out(multiplexer_4_out), .sel(instr[5:2]));  // open: en
  Multiplexer #(.select(2), .width(32)) multiplexer_5 (
    .in0({32{1'b0}}), .in1({32{1'b0}}), .in2({32{1'b0}}), .in3(multiplexer_4_out), .out(Imm), .sel(instr[1:0]));  // open: en

  // Notes on the sheet:
  //   addi, lw
  //   jalr
  //   sw
  //   branch
  //   jal
  //   lui, auipc
  //   opcode[6]
  //   opcode[2:5]
  //   opcode[0:1]
endmodule
