// Logisim project alu.circ as structural Verilog: 1 circuit, main circuit main
module main (
  input  [31:0] in0,
  input  [31:0] in1,
  input  [2:0] op,
  output [31:0] out
);

  wire [31:0] adder_1_out, and_1_out, or_1_out, subtractor_1_out;

  assign and_1_out = in0 & in1;  // AND_Gate and_1, 32 bits wide
  assign or_1_out = in1 | in0;  // OR_Gate or_1, 32 bits wide
  Adder #(.width(32)) adder_1 (.a(in1), .b(in0), .out(adder_1_out));  // open: cin, cout
  Subtractor #(.width(32)) subtractor_1 (.a(in0), .b(in1), .out(subtractor_1_out));  // open: bin, bout
  Multiplexer #(.select(3), .width(32)) multiplexer_1 (
    .in0(and_1_out), .in1(or_1_out), .in2(adder_1_out), .in6(subtractor_1_out), .out(out), .sel(op));  // open: in3, in4, in5, in7, en
endmodule
