// Logisim project alu_control.circ as structural Verilog: 1 circuit, main circuit main
module main (
  input  [1:0] ALU_op,
  input  [31:0] instr,
  output [2:0] op
);

  wire [2:0] multiplexer_1_out, multiplexer_2_out, multiplexer_3_out, multiplexer_4_out;

  Multiplexer #(.width(3)) multiplexer_1 (
    .in0(3'b010), .in1(3'b110), .out(multiplexer_1_out), .sel(instr[26]));  // open: en
  Multiplexer #(.width(3)) multiplexer_2 (
    .in0(3'b001), .in1(3'b110), .out(multiplexer_2_out), .sel(instr[26]));  // open: en
  Multiplexer #(.width(3)) multiplexer_3 (
    .in0(3'b000), .in1(3'b110), .out(multiplexer_3_out), .sel(instr[26]));  // open: en
  Multiplexer #(.select(3), .width(3)) multiplexer_4 (
    .in0(multiplexer_1_out), .in6(multiplexer_2_out), .in7(multiplexer_3_out), .out(multiplexer_4_out),
    .sel(instr[14:12]));  // open: in1, in2, in3, in4, in5, en
  Multiplexer #(.select(2), .width(3)) multiplexer_5 (
    .in0(3'b010), .in1(3'b110), .in2(multiplexer_4_out), .in3(3'b110), .out(op), .sel(ALU_op));  // open: en

  // Notes on the sheet:
  //   ADD
  //   SUB
  //   funct3
  //   funct7[5]
  //   OR
  //   AND
  //   ADD
  //   SUB
endmodule
