// Logisim project branch.circ as structural Verilog: 1 circuit, main circuit main
module main (
  input  ctrl_branch,
  input  [2:0] funct3,
  input  [31:0] in0,
  input  [31:0] in1,
  output branch
);

  wire comparator_1_eq, comparator_1_lt, multiplexer_1_out, not_1_out, not_2_out;

  Comparator #(.width(32)) comparator_1 (.a(in0), .b(in1), .eq(comparator_1_eq), .lt(comparator_1_lt));  // open: gt
  not not_1 (not_1_out, comparator_1_eq);
  not not_2 (not_2_out, comparator_1_lt);
  Multiplexer #(.select(3)) multiplexer_1 (
    .in0(comparator_1_eq), .in1(not_1_out), .in2(1'b0), .in3(1'b0), .in4(comparator_1_lt), .in5(not_2_out),
    .in6(1'b0), .in7(1'b0), .out(multiplexer_1_out), .sel(funct3));  // open: en
  and and_1 (branch, ctrl_branch, multiplexer_1_out);
endmodule
