// Logisim project control.circ as structural Verilog: 1 circuit, main circuit main
module main (
  input  [6:0] opcode,
  output branch,
  output [1:0] ALU_op,
  output jal,
  output jalr,
  output m_rd,
  output m_wr,
  output [1:0] a_sel,
  output [1:0] b_sel,
  output [1:0] wb_sel,
  output rf_wr
);

  wire comparator_3_eq, comparator_8_eq;

  Comparator #(.width(7)) comparator_1 (.a(opcode), .b(7'b1100011), .eq(ALU_op[0]));  // open: gt, lt
  Comparator #(.width(7)) comparator_2 (.a(opcode), .b(7'b0110011), .eq(ALU_op[1]));  // open: gt, lt
  Comparator #(.width(7)) comparator_3 (.a(opcode), .b(7'b0010011), .eq(comparator_3_eq));  // open: gt, lt
  Comparator #(.width(7)) comparator_4 (.a(opcode), .b(7'b1101111), .eq(jal));  // open: gt, lt
  Comparator #(.width(7)) comparator_5 (.a(opcode), .b(7'b1100111), .eq(jalr));  // open: gt, lt
  Comparator #(.width(7)) comparator_6 (.a(opcode), .b(7'b0000011), .eq(m_rd));  // open: gt, lt
  Comparator #(.width(7)) comparator_7 (.a(opcode), .b(7'b0100011), .eq(m_wr));  // open: gt, lt
  Comparator #(.width(7)) comparator_8 (.a(opcode), .b(7'b0010111), .eq(comparator_8_eq));  // open: gt, lt
  Comparator #(.width(7)) comparator_9 (.a(opcode), .b(7'b0110111), .eq(a_sel[1]));  // open: gt, lt
  or or_1 (b_sel[0], comparator_3_eq, m_rd, m_wr, comparator_8_eq, a_sel[1]);
  or or_2 (b_sel[1], jal, jalr);
  or or_3 (a_sel[0], jal, jalr, comparator_8_eq);
  or or_4 (rf_wr, ALU_op[1], comparator_3_eq, jal, jalr, m_rd, comparator_8_eq, a_sel[1]);

  assign branch = ALU_op[0];
  assign wb_sel = {1'b0, m_rd};

  // Notes on the sheet:
  //   branch
  //   add
  //   addi
  //   jal
  //   jalr
  //   lw
  //   sw
  //   auipc
  //   lui
endmodule
