// Logisim project data_memory.circ as structural Verilog: 1 circuit, main circuit main
module main (
  input  [31:0] wd,
  input  [31:0] wa,
  input  clk,
  input  m_wr,
  input  m_rd,
  output [31:0] out
);

  wire not_1_out;
  wire [7:0] bitselector_1_out;
  wire [31:0] divider_1_out, ram_1_data;

  not not_1 (not_1_out, m_wr);
  Divider #(.width(32)) divider_1 (.a(wa), .b(32'h4), .out(divider_1_out));  // open: upper, rem
  BitSelector #(.width(32), .group(8)) bitselector_1 (.in(divider_1_out), .out(bitselector_1_out), .sel(2'b00));
  RAM #(.dataWidth(32)) ram_1 (
    .addr(bitselector_1_out), .data(ram_1_data), .clk(clk), .ld(not_1_out));  // open: sel, clr
  Multiplexer #(.width(32)) multiplexer_1 (.in0(wd), .out(ram_1_data), .sel(not_1_out));  // open: in1, en
  Multiplexer #(.width(32)) multiplexer_2 (.in1(ram_1_data), .out(out), .sel(m_rd));  // open: in0, en
endmodule
