// Logisim project hazard_unit.circ as structural Verilog: 1 circuit, main circuit main
module main (
  input  [4:0] rde,
  input  [4:0] rs1,
  input  [4:0] rs2,
  input  m_rd_e,
  input  branch,
  input  jump,
  output dstall,
  output fstall,
  output dflush,
  output eflush
);

  wire comparator_1_eq, comparator_2_eq, comparator_3_eq, not_1_out, or_2_out;

  Comparator #(.width(5)) comparator_1 (.a(rde), .b({5{1'b0}}), .eq(comparator_1_eq));  // open: gt, lt
  Comparator #(.width(5)) comparator_2 (.a(rde), .b(rs1), .eq(comparator_2_eq));  // open: gt, lt
  Comparator #(.width(5)) comparator_3 (.a(rde), .b(rs2), .eq(comparator_3_eq));  // open: gt, lt
  or or_1 (dflush, branch, jump);
  not not_1 (not_1_out, comparator_1_eq);
  or or_2 (or_2_out, comparator_2_eq, comparator_3_eq);
  and and_1 (dstall, not_1_out, or_2_out, m_rd_e);

  assign eflush = dflush;
  assign fstall = dstall;
endmodule
