// Logisim project instr_memory.circ as structural Verilog: 1 circuit, main circuit main
module main (
  input  [31:0] addr,
  input  clk,
  output [31:0] instr
);

  wire [7:0] bitselector_1_out;
  wire [31:0] divider_1_out;

  BitSelector #(.width(32), .group(8)) bitselector_1 (.in(divider_1_out), .out(bitselector_1_out), .sel(2'b00));
  Divider #(.width(32)) divider_1 (.a(addr), .b(32'h4), .out(divider_1_out));  // open: upper, rem
  RAM #(.dataWidth(32)) ram_1 (.addr(bitselector_1_out), .data(instr), .clk(clk));  // open: sel, ld, clr
endmodule
