// Logisim project mux.circ as structural Verilog: 8 circuits, main circuit MUX 2 North
module MUX_2_North (
  input  [31:0] in_1,
  input  [31:0] in_2,
  input  in_3,
  output [31:0] out_4
);

  Multiplexer #(.width(32)) multiplexer_1 (.in0(in_1), .in1(in_2), .out(out_4), .sel(in_3));  // open: en
endmodule

module MUX_2_North_reverse (
  input  [31:0] in_1,
  input  [31:0] in_2,
  input  in_3,
  output [31:0] out_4
);

  Multiplexer #(.width(32)) multiplexer_1 (.in0(in_1), .in1(in_2), .out(out_4), .sel(in_3));  // open: en
endmodule

module MUX_2_South (
  input  [31:0] in_1,
  input  [31:0] in_2,
  input  in_3,
  output [31:0] out_4
);

  Multiplexer #(.width(32)) multiplexer_1 (.in0(in_1), .in1(in_2), .out(out_4), .sel(in_3));  // open: en
endmodule

module MUX_2_South_reverse (
  input  [31:0] in_1,
  input  [31:0] in_2,
  input  in_3,
  output [31:0] out_4
);

  Multiplexer #(.width(32)) multiplexer_1 (.in0(in_1), .in1(in_2), .out(out_4), .sel(in_3));  // open: en
endmodule

module MUX_3_North (
  input  [31:0] in_1,
  input  [31:0] in_2,
  input  [31:0] in_3,
  input  [1:0] in_4,
  output [31:0] out_5
);

  Multiplexer #(.select(2), .width(32)) multiplexer_1 (
    .in0(in_1), .in1(in_2), .in2(in_3), .in3({32{1'b0}}), .out(out_5), .sel(in_4));  // open: en
endmodule

module MUX_3_North_reverse (
  input  [31:0] in_1,
  input  [31:0] in_2,
  input  [31:0] in_3,
  input  [1:0] in_4,
  output [31:0] out_5
);

  Multiplexer #(.select(2), .width(32)) multiplexer_1 (
    .in0(in_1), .in1(in_2), .in2(in_3), .in3({32{1'b0}}), .out(out_5), .sel(in_4));  // open: en
endmodule

module MUX_3_South (
  input  [31:0] in_1,
  input  [31:0] in_2,
  input  [31:0] in_3,
  input  [1:0] in_4,
  output [31:0] out_5
);

  Multiplexer #(.select(2), .width(32)) multiplexer_1 (
    .in0(in_1), .in1(in_2), .in2(in_3), .in3({32{1'b0}}), .out(out_5), .sel(in_4));  // open: en
endmodule

module MUX_3_South_reverse (
  input  [31:0] in_1,
  input  [31:0] in_2,
  input  [31:0] in_3,
  input  [1:0] in_4,
  output [31:0] out_5
);

  Multiplexer #(.select(2), .width(32)) multiplexer_1 (
    .in0(in_1), .in1(in_2), .in2(in_3), .in3({32{1'b0}}), .out(out_5), .sel(in_4));  // open: en
endmodule
