// Logisim project regfile.circ as structural Verilog: 4 circuits, main circuit main
module main (
  input  [31:0] wd,
  input  clk,
  input  we,
  input  [4:0] wa,
  input  [4:0] ra0,
  input  clear,
  input  [4:0] ra1,
  input  [4:0] ra2,
  output [31:0] rd0,
  output [31:0] rd1,
  output [31:0] rd2
);

  wire and_1_out, and_2_out, and_3_out, equal_1_out_3, equal_2_out_3, equal_3_out_3, not_equal_1_out_3,
       not_equal_2_out_3, not_equal_3_out_3;
  wire [31:0] multiplexer_1_out, multiplexer_2_out, multiplexer_3_out, reg_1_out, reg_2_out, reg_3_out,
       reg_4_out, reg_5_out, reg_6_out, reg_7_out, reg_8_out, reg_9_out, reg_10_out, reg_11_out, reg_12_out,
       reg_13_out, reg_14_out, reg_15_out, reg_16_out, reg_17_out, reg_18_out, reg_19_out, reg_20_out,
       reg_21_out, reg_22_out, reg_23_out, reg_24_out, reg_25_out, reg_26_out, reg_27_out, reg_28_out,
       reg_29_out, reg_30_out, reg_31_out;

  REG reg_1 (.wd(wd), .en(we), .wa(5'b00110), .num(wa), .clk(clk), .out(reg_1_out), .clear(clear));
  REG reg_2 (.wd(wd), .en(we), .wa(5'b01100), .num(wa), .clk(clk), .out(reg_2_out), .clear(clear));
  REG reg_3 (.wd(wd), .en(we), .wa(5'b10010), .num(wa), .clk(clk), .out(reg_3_out), .clear(clear));
  REG reg_4 (.wd(wd), .en(we), .wa(5'b11000), .num(wa), .clk(clk), .out(reg_4_out), .clear(clear));
  REG reg_5 (.wd(wd), .en(we), .wa(5'b11110), .num(wa), .clk(clk), .out(reg_5_out), .clear(clear));
  REG reg_6 (.wd(wd), .en(we), .wa({5{1'b1}}), .num(wa), .clk(clk), .out(reg_6_out), .clear(clear));
  REG reg_7 (.wd(wd), .en(we), .wa(5'b00101), .num(wa), .clk(clk), .out(reg_7_out), .clear(clear));
  REG reg_8 (.wd(wd), .en(we), .wa(5'b01011), .num(wa), .clk(clk), .out(reg_8_out), .clear(clear));
  REG reg_9 (.wd(wd), .en(we), .wa(5'b10001), .num(wa), .clk(clk), .out(reg_9_out), .clear(clear));
  REG reg_10 (.wd(wd), .en(we), .wa(5'b10111), .num(wa), .clk(clk), .out(reg_10_out), .clear(clear));
  REG reg_11 (.wd(wd), .en(we), .wa(5'b11101), .num(wa), .clk(clk), .out(reg_11_out), .clear(clear));
  REG reg_12 (.wd(wd), .en(we), .wa(5'b00100), .num(wa), .clk(clk), .out(reg_12_out), .clear(clear));
  REG reg_13 (.wd(wd), .en(we), .wa(5'b01010), .num(wa), .clk(clk), .out(reg_13_out), .clear(clear));
  REG reg_14 (.wd(wd), .en(we), .wa(5'b10000), .num(wa), .clk(clk), .out(reg_14_out), .clear(clear));
  REG reg_15 (.wd(wd), .en(we), .wa(5'b10110), .num(wa), .clk(clk), .out(reg_15_out), .clear(clear));
  REG reg_16 (.wd(wd), .en(we), .wa(5'b11100), .num(wa), .clk(clk), .out(reg_16_out), .clear(clear));
  REG reg_17 (.wd(wd), .en(we), .wa(5'b00011), .num(wa), .clk(clk), .out(reg_17_out), .clear(clear));
  REG reg_18 (.wd(wd), .en(we), .wa(5'b01001), .num(wa), .clk(clk), .out(reg_18_out), .clear(clear));
  REG reg_19 (.wd(wd), .en(we), .wa(5'b01111), .num(wa), .clk(clk), .out(reg_19_out), .clear(clear));
  REG reg_20 (.wd(wd), .en(we), .wa(5'b10101), .num(wa), .clk(clk), .out(reg_20_out), .clear(clear));
  REG reg_21 (.wd(wd), .en(we), .wa(5'b11011), .num(wa), .clk(clk), .out(reg_21_out), .clear(clear));
  REG reg_22 (.wd(wd), .en(we), .wa(5'b00010), .num(wa), .clk(clk), .out(reg_22_out), .clear(clear));
  REG reg_23 (.wd(wd), .en(we), .wa(5'b01000), .num(wa), .clk(clk), .out(reg_23_out), .clear(clear));
  REG reg_24 (.wd(wd), .en(we), .wa(5'b01110), .num(wa), .clk(clk), .out(reg_24_out), .clear(clear));
  REG reg_25 (.wd(wd), .en(we), .wa(5'b10100), .num(wa), .clk(clk), .out(reg_25_out), .clear(clear));
  REG reg_26 (.wd(wd), .en(we), .wa(5'b11010), .num(wa), .clk(clk), .out(reg_26_out), .clear(clear));
  REG reg_27 (.wd(wd), .en(we), .wa(5'b00001), .num(wa), .clk(clk), .out(reg_27_out), .clear(clear));
  REG reg_28 (.wd(wd), .en(we), .wa(5'b00111), .num(wa), .clk(clk), .out(reg_28_out), .clear(clear));
  REG reg_29 (.wd(wd), .en(we), .wa(5'b01101), .num(wa), .clk(clk), .out(reg_29_out), .clear(clear));
  REG reg_30 (.wd(wd), .en(we), .wa(5'b10011), .num(wa), .clk(clk), .out(reg_30_out), .clear(clear));
  REG reg_31 (.wd(wd), .en(we), .wa(5'b11001), .num(wa), .clk(clk), .out(reg_31_out), .clear(clear));
  Multiplexer #(.select(5), .width(32)) multiplexer_1 (
    .in0({32{1'b0}}), .in1(reg_27_out), .in2(reg_22_out), .in3(reg_17_out), .in4(reg_12_out),
    .in5(reg_7_out), .in6(reg_1_out), .in7(reg_28_out), .in8(reg_23_out), .in9(reg_18_out),
    .in10(reg_13_out), .in11(reg_8_out), .in12(reg_2_out), .in13(reg_29_out), .in14(reg_24_out),
    .in15(reg_19_out), .in16(reg_14_out), .in17(reg_9_out), .in18(reg_3_out), .in19(reg_30_out),
    .in20(reg_25_out), .in21(reg_20_out), .in22(reg_15_out), .in23(reg_10_out), .in24(reg_4_out),
    .in25(reg_31_out), .in26(reg_26_out), .in27(reg_21_out), .in28(reg_16_out), .in29(reg_11_out),
    .in30(reg_5_out), .in31(reg_6_out), .out(multiplexer_1_out), .sel(ra0));  // open: en
  Multiplexer #(.select(5), .width(32)) multiplexer_2 (
    .in0({32{1'b0}}), .in1(reg_27_out), .in2(reg_22_out), .in3(reg_17_out), .in4(reg_12_out),
    .in5(reg_7_out), .in6(reg_1_out), .in7(reg_28_out), .in8(reg_23_out), .in9(reg_18_out),
    .in10(reg_13_out), .in11(reg_8_out), .in12(reg_2_out), .in13(reg_29_out), .in14(reg_24_out),
    .in15(reg_19_out), .in16(reg_14_out), .in17(reg_9_out), .in18(reg_3_out), .in19(reg_30_out),
    .in20(reg_25_out), .in21(reg_20_out), .in22(reg_15_out), .in23(reg_10_out), .in24(reg_4_out),
    .in25(reg_31_out), .in26(reg_26_out), .in27(reg_21_out), .in28(reg_16_out), .in29(reg_11_out),
    .in30(reg_5_out), .in31(reg_6_out), .out(multiplexer_2_out), .sel(ra1));  // open: en
  Multiplexer #(.select(5), .width(32)) multiplexer_3 (
    .in0({32{1'b0}}), .in1(reg_27_out), .in2(reg_22_out), .in3(reg_17_out), .in4(reg_12_out),
    .in5(reg_7_out), .in6(reg_1_out), .in7(reg_28_out), .in8(reg_23_out), .in9(reg_18_out),
    .in10(reg_13_out), .in11(reg_8_out), .in12(reg_2_out), .in13(reg_29_out), .in14(reg_24_out),
    .in15(reg_19_out), .in16(reg_14_out), .in17(reg_9_out), .in18(reg_3_out), .in19(reg_30_out),
    .in20(reg_25_out), .in21(reg_20_out), .in22(reg_15_out), .in23(reg_10_out), .in24(reg_4_out),
    .in25(reg_31_out), .in26(reg_26_out), .in27(reg_21_out), .in28(reg_16_out), .in29(reg_11_out),
    .in30(reg_5_out), .in31(reg_6_out), .out(multiplexer_3_out), .sel(ra2));  // open: en
  equal equal_1 (.in_1(ra0), .in_2(wa), .out_3(equal_1_out_3));
  not_equal not_equal_1 (.in_1(wa), .in_2({5{1'b0}}), .out_3(not_equal_1_out_3));
  equal equal_2 (.in_1(ra1), .in_2(wa), .out_3(equal_2_out_3));
  not_equal not_equal_2 (.in_1(wa), .in_2({5{1'b0}}), .out_3(not_equal_2_out_3));
  equal equal_3 (.in_1(ra2), .in_2(wa), .out_3(equal_3_out_3));
  not_equal not_equal_3 (.in_1(wa), .in_2({5{1'b0}}), .out_3(not_equal_3_out_3));
  and and_1 (and_1_out, equal_1_out_3, we, not_equal_1_out_3);
  Multiplexer #(.width(32)) multiplexer_4 (.in0(multiplexer_1_out), .in1(wd), .out(rd0), .sel(and_1_out));  // open: en
  and and_2 (and_2_out, equal_2_out_3, we, not_equal_2_out_3);
  Multiplexer #(.width(32)) multiplexer_5 (.in0(multiplexer_2_out), .in1(wd), .out(rd1), .sel(and_2_out));  // open: en
  and and_3 (and_3_out, equal_3_out_3, we, not_equal_3_out_3);
  Multiplexer #(.width(32)) multiplexer_6 (.in0(multiplexer_3_out), .in1(wd), .out(rd2), .sel(and_3_out));  // open: en
endmodule

module REG (
  input  [31:0] wd,
  input  en,
  input  [4:0] wa,
  input  [4:0] num,
  input  clk,
  input  clear,
  output [31:0] out
);

  wire equal_1_out_3, multiplexer_1_out;

  equal equal_1 (.in_1(wa), .in_2(num), .out_3(equal_1_out_3));
  Multiplexer multiplexer_1 (.in0(1'b0), .in1(equal_1_out_3), .out(multiplexer_1_out), .sel(en));  // open: en
  Register #(.width(32)) register_1 (.D(wd), .en(multiplexer_1_out), .Q(out), .clk(clk), .clr(clear));
endmodule

module equal (
  input  [4:0] in_1,
  input  [4:0] in_2,
  output out_3
);

  Comparator #(.width(5)) comparator_1 (.a(in_1), .b(in_2), .eq(out_3));  // open: gt, lt
endmodule

module not_equal (
  input  [4:0] in_1,
  input  [4:0] in_2,
  output out_3
);

  wire equal_1_out_3;

  equal equal_1 (.in_1(in_1), .in_2(in_2), .out_3(equal_1_out_3));
  not not_1 (out_3, equal_1_out_3);
endmodule
