// Logisim project tmp.circ as structural Verilog: 1 circuit, main circuit main
module main (
  input  [31:0] in_1,
  input  [31:0] in_2,
  input  [31:0] in_3,
  input  [1:0] in_4,
  output [31:0] out_5
);

  Multiplexer #(.select(2), .width(32)) multiplexer_1 (
    .in0(in_1), .in1(in_2), .in2(in_3), .in3({32{1'b0}}), .out(out_5), .sel(in_4));  // open: en
endmodule
